// Logisim project lab2.circ as structural Verilog: 2 circuits, main circuit 4-bit_RCA
module Full_Adder (
  input  A,
  input  B,
  input  Cin,
  output Sum,
  output Cout
);

  wire and_2_p1, or_1_p1, or_1_p2;

  // XOR_Gate xor_1: pin names not known; wires that end beside it: A, B
  // AND_Gate and_1: pin names not known; wires that end beside it: A, B
  // AND_Gate and_2: pin names not known; wires that end beside it: and_2_p1, Cin
  // XOR_Gate xor_2: pin names not known; wires that end beside it: and_2_p1, Cin
  // OR_Gate or_1: pin names not known; wires that end beside it: or_1_p1, or_1_p2, or_1_p1, or_1_p2
endmodule

module _4_bit_RCA (
  input  A0,
  input  A1,
  input  A2,
  input  A3,
  input  B0,
  input  B1,
  input  B2,
  input  B3,
  input  Cin,
  output S0,
  output S1,
  output S2,
  output S3,
  output Cout
);

  wire FA0_p5, FA1_p5, FA2_p5;

  // Full_Adder_part FA0: pin names not known; wires that end beside it: A0, B0, Cin, S0, FA0_p5
  // Full_Adder_part FA1: pin names not known; wires that end beside it: A1, B1, FA0_p5, S1, FA1_p5
  // Full_Adder_part FA2: pin names not known; wires that end beside it: A2, B2, FA1_p5, S2, FA2_p5
  // Full_Adder_part FA3: pin names not known; wires that end beside it: A3, B3, FA2_p5, S3, Cout
endmodule
